# Fritzing sketch schematic (saved by Fritzing 0.9.2b)

parts:
  R1 = Resistor [tolerance=±5% resistance=4.7k package=THT]  # not connected
  DS1 = DS18B20 1-Wire Temperature Sensor Probe
  DS2 = DS18B20 1-Wire Temperature Sensor Probe
  DS3 = DS18B20 1-Wire Temperature Sensor Probe
  Part1 = Arduino Uno (Rev3)
  R2 = Photocell (LDR) [package=THT]
  R3 = Resistor [tolerance=±5% resistance=330 package=THT]
  M1 = DC Motor
  Mod1 = Solar Charge Controller [part_number="KLD Series Solar Charge Controller PWM" package=PWM-Model]
  U1 = 2-Channel 5v Relay Shield [package=relay-2ch5v10a]
  SD_card_module1 = SD Card Module
  BAT1 = 12 battery [package=battery]
  Part3 = Solar Panel [package="Renogy 50 Watts 12 Volt Monocrystalline Bendable Solar Panel"]
  Part4 = FC-28 Soil Hygrometer Module - Probe
  Part5 = FC-28 Soil Hygrometer Module
  M2 = DC Motor
  Part6 = FC-28 Soil Hygrometer Module - Probe
  Part7 = FC-28 Soil Hygrometer Module
  S1 = Reed switch [package=THT]
  YL-83_-_Detection_Board1 = YL-83 Rain Sensor - Detection Board
  YL-83_-_Control_Board1 = YL-83 Rain Sensor - Control Board
  R4 = Resistor [tolerance=±5% resistance=47k package=THT]
  R5 = Resistor [tolerance=±5% resistance=22k package=THT]
  R6 = Resistor [tolerance=±5% resistance=220 package=THT]
  LED1 = LED - 5mm [color="Red (633nm)" package="5 mm [THT]"]
  S2 = Reed switch [package=THT]

nets:
  GND: DS1.GND, DS2.GND, DS3.GND, Part1.GND, Mod1.Connector_6, SD_card_module1.GND
  N1: DS1.DQ, DS2.DQ, DS3.DQ, Part1.D2
  VDD: DS1.VDD, DS2.VDD, DS3.VDD, Part1.5V, SD_card_module1.+5, Part5.VCC
  N2: Part1.A0, Part5.AO
  N3: Part1.A1, Part7.AO
  N4: Part1.A2, YL-83_-_Control_Board1.AO
  N5: Part1.D8, U1.IN2
  N6: Part1.D9_PWM, R6.Pin_0
  N7: Part1.D10_PWM/SS, SD_card_module1.CS
  N8: Part1.D11_PWM/MOSI, SD_card_module1.MOSI
  N9: Part1.D12/MISO, SD_card_module1.MISO
  N10: Part1.D13/SCK, SD_card_module1.SCK
  N11: Part1.D5_PWM, S2.pin_2
  N12: Part1.D6_PWM, S1.pin_2
  N13: Part1.D7, U1.IN1
  N14: Part1.VIN, Mod1.Connector_5
  N15: R2.pin_1, R3.Pin_0
  N16: M1.pin_1, U1.K2-On
  N17: M1.pin_2, U1.GND
  N18: Mod1.Connector_1, Part3.Connector_1
  N19: Mod1.Connector_2, Part3.Connector_2
  N20: Mod1.Connector_3, BAT1.+
  N21: Mod1.Connector_4, BAT1.-, R4.Pin_0
  N22: U1.K1-On, M2.pin_1
  N23: Part4.POS, Part5.POS
  N24: Part4.NEG, Part5.NEG
  N25: Part6.POS, Part7.POS
  N26: Part6.NEG, Part7.NEG
  N27: YL-83_-_Detection_Board1.POS, YL-83_-_Control_Board1.POS
  N28: YL-83_-_Detection_Board1.NEG, YL-83_-_Control_Board1.NEG
  N29: R4.Pin_1, R5.Pin_0
  N30: R6.Pin_1, LED1.anode

custom parts:
  Solar Charge Controller: PWM-Solar Charge Controller
  2-Channel 5v Relay Shield: 2 Channel 5v Relay Shield w. 2x SPD-06VDC-SD-C
  SD Card Module: SD Card Module Slot Socket Reader For Arduino ARM MCU
  12 battery: 12V lead acid type battery, like the Husqvarna YTH2448 12V 35AH battery. This is the mini version 1/4 the size of the actual battery to be closer to typical breadboard parts (around 2in wide rathher than 7in). The pads in pcb are sized to accomidate up to 14ga wire (as these batterys will deliver high currents.)
  Solar Panel: Renogy 50 Watts 12 Volt Solar Panel
  FC-28 Soil Hygrometer Module - Probe: The FC-28 is a soil hygrometer module that uses the Texas Instruments LM393 comparator chip to provide an analog measurement of soil humidity.
  FC-28 Soil Hygrometer Module: The FC-28 is a soil hygrometer module that uses the Texas Instruments LM393 comparator chip to provide an analog measurement of soil humidity. The digital output is high when soil moisture is over a certain threshold, as determined by adjusting the potentiometer.
  YL-83 Rain Sensor - Detection Board: The YL-83 is a rain sensor that has more resistance when dry and less resistance when wet. The module runs at 5V.
  YL-83 Rain Sensor - Control Board: The YL-83 is a rain sensor that has more resistance when dry and less resistance when wet. The module runs at 5V.
